// Logisim project dsproject.circ as structural Verilog: 1 circuit, main circuit main
module main (
  input  in_1
);

  wire and_1_out, and_2_out, and_3_out, and_4_out, and_5_out, and_6_out, and_7_out, and_8_out, and_9_out,
       and_10_out, and_11_out, and_12_out, and_13_out, and_14_out, and_15_out, and_16_out, button_1_out,
       j_k_ff_1_q, j_k_ff_2_q, j_k_ff_3_q, j_k_ff_4_q, j_k_ff_4_qn, not_1_out, not_2_out, not_3_out,
       not_4_out, not_5_out, not_6_out, not_7_out, not_8_out, not_9_out, or_1_out, or_2_out, or_3_out,
       or_4_out, or_5_out, or_6_out, or_7_out, or_8_out, or_9_out, or_10_out, or_11_out, undriven,
       undriven_2, undriven_3, undriven_4, undriven_5, undriven_6, undriven_7, xnor_1_out, xor_1_out;

  not not_1 (not_1_out, button_1_out);
  J_K_Flip_Flop j_k_ff_1 (.J(in_1), .clk(not_1_out), .K(in_1), .Q(j_k_ff_1_q));  // open: Qn, preset, en, reset
  J_K_Flip_Flop j_k_ff_2 (.J(j_k_ff_4_qn), .clk(not_2_out), .K(in_1), .Q(j_k_ff_2_q));  // open: Qn, preset, en, reset
  not not_2 (not_2_out, j_k_ff_1_q);
  Button button_1 (.out(button_1_out));
  J_K_Flip_Flop j_k_ff_3 (.J(in_1), .clk(not_3_out), .K(in_1), .Q(j_k_ff_3_q));  // open: Qn, preset, en, reset
  not not_3 (not_3_out, j_k_ff_2_q);
  _7_Segment_Display u_7_segment_display_1 (
    .g(or_2_out), .f(or_1_out), .a(or_10_out), .b(or_6_out), .e(and_2_out), .d(or_9_out), .c(or_5_out));  // open: dp
  and and_1 (and_1_out, j_k_ff_2_q, j_k_ff_3_q);
  J_K_Flip_Flop j_k_ff_4 (
    .J(and_1_out), .clk(not_4_out), .K(in_1), .Q(j_k_ff_4_q), .Qn(j_k_ff_4_qn));  // open: preset, en, reset
  not not_4 (not_4_out, j_k_ff_1_q);
  and and_2 (and_2_out, or_3_out, not_5_out);
  and and_3 (and_3_out, or_4_out, not_7_out);
  or or_1 (or_1_out, and_3_out, j_k_ff_4_q, and_4_out);
  and and_4 (and_4_out, not_5_out, j_k_ff_3_q);
  xor xor_1 (xor_1_out, j_k_ff_2_q, j_k_ff_3_q);
  or or_2 (or_2_out, xor_1_out, and_5_out, j_k_ff_4_q);
  and and_5 (and_5_out, j_k_ff_3_q, not_5_out);
  not not_5 (not_5_out, j_k_ff_1_q);
  and and_6 (and_6_out, not_7_out, not_6_out);
  or or_3 (or_3_out, and_6_out, j_k_ff_2_q);
  or or_4 (or_4_out, j_k_ff_3_q, not_5_out);
  not not_6 (not_6_out, j_k_ff_3_q);
  not not_7 (not_7_out, j_k_ff_2_q);
  not not_8 (not_8_out, j_k_ff_4_q);
  and and_7 (and_7_out, not_8_out, not_6_out);
  xnor xnor_1 (xnor_1_out, j_k_ff_2_q, j_k_ff_1_q);
  or or_5 (or_5_out, j_k_ff_3_q, not_7_out, j_k_ff_4_q, j_k_ff_1_q);
  and and_8 (and_8_out, j_k_ff_2_q, not_8_out);
  and and_9 (and_9_out, not_7_out, not_5_out);
  or or_6 (or_6_out, and_7_out, j_k_ff_4_q, xnor_1_out);
  not not_9 (not_9_out, not_6_out);
  and and_10 (and_10_out, j_k_ff_1_q, not_7_out, not_9_out);
  and and_11 (and_11_out, not_6_out, or_7_out);
  or or_7 (or_7_out, and_8_out, and_9_out);
  and and_12 (and_12_out, not_5_out, j_k_ff_2_q);
  or or_8 (or_8_out, and_13_out, j_k_ff_2_q);
  and and_13 (and_13_out, j_k_ff_3_q, j_k_ff_1_q);
  and and_14 (and_14_out, not_6_out, not_7_out);
  or or_9 (or_9_out, and_10_out, j_k_ff_4_q, and_11_out, and_12_out);
  and and_15 (and_15_out, not_8_out, or_8_out);
  or or_10 (or_10_out, and_15_out, and_16_out);
  and and_16 (and_16_out, and_14_out, or_11_out);
  or or_11 (or_11_out, j_k_ff_4_q, not_5_out);
  _7_Segment_Display u_7_segment_display_2 (
    .g(undriven), .f(undriven_3), .a(undriven_5), .b(undriven_7), .e(undriven_2), .d(undriven_4),
    .c(undriven_6));  // open: dp

  // Notes on the sheet:
  //   w
  //   x
  //   y
  //   z
  //   a
  //   b
  //   c
  //   d
  //   e
  //   f
  //   g
  //   g
  //   f
  //   d
  //   e
  //   a
  //   b
  //   c
endmodule
