// Logisim project incrementer.circ as structural Verilog: 1 circuit, main circuit main
module main (
  input  [15:0] Input,
  output [15:0] Output
);

  wire Reset_out;
  wire [15:0] adder_1_out;

  // Probe on Input
  Adder #(.width(16)) adder_1 (.out(adder_1_out));  // open: a, b, cin, cout
  Button Reset (.out(Reset_out));
  Register #(.width(16)) register_1 (.Q(Output));  // open: D, en, clk, clr
  Clock clock_1 (.out(Output[0]));
  // NOT_Gate not_1: pin names not known; wires that end beside it: Reset_out
  // Probe on Output
  // Pins of 1 and 16 bits meet at Output
  // also tied to GND on the sheet: {adder_1_out[1], adder_1_out[2], adder_1_out[3], adder_1_out[4], adder_1_out[5], adder_1_out[6], adder_1_out[7], adder_1_out[8], adder_1_out[9], adder_1_out[10], adder_1_out[11], adder_1_out[12], adder_1_out[13], adder_1_out[14], adder_1_out[15]}
  // also tied to VCC on the sheet: adder_1_out[0]
endmodule
